# Fritzing sketch Untitled Sketch 3 (saved by Fritzing 0.9.3b)
circuit board: 11.6981cm x 6.37822cm
breadboards: 1

parts:
  U1 = NodeMCU V1.0
  DHT1 = DHT11 Humitidy and Temperature Sensor
  Componente1 = BH1750
  Componente2 = FC-28 Soil Hygrometer Module
  KY-1 = Keyes Relay [package=THT]
  KY-2 = Keyes Relay [package=THT]
  LCM1602_IIC1 = LCM1602 IIC [part_number="LCM1602 IIC" chip_label="LCM1602 IIC" package="DIP (Dual Inline) [THT]"]

nets:
  N1: U1.D0, LCM1602_IIC1.SCL
  N2: U1.D1, Componente1.SCL
  N3: U1.D2, Componente1.SDA, LCM1602_IIC1.SDA
  N4: U1.D3, KY-2.signal
  N5: U1.D4, KY-1.signal
  3V3: U1.3V3, DHT1.VDD, Componente1.VCC
  GND: U1.GND, DHT1.GND, Componente1.GND, Componente2.GND, KY-1.ground, KY-2.ground, LCM1602_IIC1.GND
  N6: U1.D5, DHT1.DATA
  VIN: U1.Vin, KY-1.power, KY-2.power, LCM1602_IIC1.VCC
  N7: U1.CLK, Componente2.VCC
  N8: U1.A0, Componente2.AO

custom parts:
  NodeMCU V1.0: ESP8266 based NodeMCU
  DHT11 Humitidy and Temperature Sensor: DHT11 Humidity and Temperature Sensor
  BH1750: Light Sensor
  FC-28 Soil Hygrometer Module: The FC-28 is a soil hygrometer module that uses the Texas Instruments LM393 comparator chip to provide an analog measurement of soil humidity. The digital output is high when soil moisture is over a certain threshold, as determined by adjusting the potentiometer.
  Keyes Relay: The Keyes 5V relay module is suitable for SCM development, home appliance control. It uses a 5V~12V TIL control signal which can control DC / AC signal.
  LCM1602 IIC: I2C-Module to use a 1602 or 2004 LCD on with the wire.h libory Serial LCD Modul
