# Fritzing sketch sketch-invernadero (saved by Fritzing 0.9.3b)
circuit board: 8.46667cm x 5.64444cm
breadboards: 1

parts:
  Sensor_Humedad_del_suelo = FC-28 Soil Hygrometer Module - Probe
  Componente3 = FC-28 Soil Hygrometer Module
  Sensor_de_luminosidad = BH1750
  Sensor_de_Tempertatura_y_Humedad = DHT11 Humitidy and Temperature Sensor
  Relay-Extractores = Keyes Relay [package=THT]
  Relay-Valvula = Keyes Relay [package=THT]
  LCD = LCD-16X2 [package=lcd-16x2_noholes]
  LCM1602_IIC1 = LCM1602 IIC [part_number="LCM1602 IIC" chip_label="LCM1602 IIC" package="DIP (Dual Inline) [THT]"]
  U1 = NodeMCU V1.0
  Part1 = Solar Charge Controller [part_number="HGX Series Solar Charge Controller PWM" package=PWM-Model]
  Part1_2 = Solar Panel [package="Renogy 50 Watts 12 Volt Monocrystalline Bendable Solar Panel"]
  BAT1 = Battery Holders [package=lipo-1100mAh]
  EXTRACTOR = Fan - Ventilador [package=THT]
  ELECTROVALVULA = DC Motor

nets:
  N1: Sensor_Humedad_del_suelo.POS, Componente3.POS
  N2: Sensor_Humedad_del_suelo.NEG, Componente3.NEG
  VCC: Componente3.VCC, Sensor_de_luminosidad.VCC, Sensor_de_Tempertatura_y_Humedad.VDD, U1.3V3
  GND: Componente3.GND, Sensor_de_luminosidad.GND, Sensor_de_Tempertatura_y_Humedad.GND, Relay-Extractores.ground, Relay-Valvula.ground, LCM1602_IIC1.GND, U1.GND, Part1.Connector_6, EXTRACTOR.GND, ELECTROVALVULA.pin_1
  N3: Componente3.AO, U1.A0
  N4: Sensor_de_luminosidad.SCL, LCM1602_IIC1.SCL, U1.D1
  N5: Sensor_de_luminosidad.SDA, LCM1602_IIC1.SDA, U1.D2
  N6: Sensor_de_Tempertatura_y_Humedad.DATA, U1.D5
  N7: Relay-Extractores.signal, U1.D4
  VCC_2: Relay-Extractores.power, Relay-Extractores.C, Relay-Valvula.power, Relay-Valvula.C, LCM1602_IIC1.VCC, U1.Vin, Part1.Connector_5
  N8: Relay-Extractores.NO, EXTRACTOR.5V
  N9: Relay-Valvula.signal, U1.D3
  N10: Relay-Valvula.NO, ELECTROVALVULA.pin_2
  N11: LCD.VSS, LCM1602_IIC1.K
  N12: LCD.VDD, LCM1602_IIC1.A
  N13: LCD.VO, LCM1602_IIC1.D7
  N14: LCD.RS, LCM1602_IIC1.D6
  N15: LCD.R_W, LCM1602_IIC1.D5
  N16: LCD.E, LCM1602_IIC1.D4
  N17: LCD.DB0, LCM1602_IIC1.D3
  N18: LCD.DB1, LCM1602_IIC1.D2
  N19: LCD.DB2, LCM1602_IIC1.D1
  N20: LCD.DB3, LCM1602_IIC1.D0
  N21: LCD.DB4, LCM1602_IIC1.E
  N22: LCD.DB5, LCM1602_IIC1.RW
  N23: LCD.DB6, LCM1602_IIC1.RS
  N24: LCD.DB7, LCM1602_IIC1.V0
  N25: LCD.A, LCM1602_IIC1.VDD
  N26: LCD.K, LCM1602_IIC1.VSS
  N27: Part1.Connector_1, Part1_2.Connector_1
  N28: Part1.Connector_2, Part1_2.Connector_2
  N29: Part1.Connector_3, BAT1.+
  N30: Part1.Connector_4, BAT1.-

custom parts:
  FC-28 Soil Hygrometer Module - Probe: The FC-28 is a soil hygrometer module that uses the Texas Instruments LM393 comparator chip to provide an analog measurement of soil humidity.
  FC-28 Soil Hygrometer Module: The FC-28 is a soil hygrometer module that uses the Texas Instruments LM393 comparator chip to provide an analog measurement of soil humidity. The digital output is high when soil moisture is over a certain threshold, as determined by adjusting the potentiometer.
  BH1750: Light Sensor
  DHT11 Humitidy and Temperature Sensor: DHT11 Humidity and Temperature Sensor
  Keyes Relay: The Keyes 5V relay module is suitable for SCM development, home appliance control. It uses a 5V~12V TIL control signal which can control DC / AC signal.
  LCM1602 IIC: I2C-Module to use a 1602 or 2004 LCD on with the wire.h libory Serial LCD Modul
  NodeMCU V1.0: ESP8266 based NodeMCU
  Solar Charge Controller: PWM-Solar Charge Controller
  Solar Panel: Renogy 50 Watts 12 Volt Solar Panel
  Fan - Ventilador: Ventilador de 2 pines, se encuentra comunmente en computadoras de escritorio
